# Fritzing sketch robot_autonomo (saved by Fritzing 1.0.3b)
breadboards: 1

parts:
  Mod1 = L298N DC motor driver
  M1 = DC Motor [voltage_(max)=6V voltage_(min)=3V]
  M2 = DC Motor [voltage_(max)=6V voltage_(min)=3V]
  VCC2 = Battery block 9V [internal_resistance=0.1Ω]
  Componente2 = Arduino Uno (Rev3)
  HC-SR04_Sensor_1 = HC-SR04 Ultrasonic Distance Sensor
  J1 = Basic Servo
  LED1 = smd LED [color="Red (633nm)" package="1206 [SMD]"]
  LED2 = smd LED [color="Green (570nm)" package="1206 [SMD]"]
  R1 = Resistor [tolerance=±5% resistance=220 package="0603 [SMD]"]
  R2 = Resistor [tolerance=±5% resistance=220 package="0603 [SMD]"]

nets:
  N1: Mod1.OUT1, M1.pin_2
  N2: Mod1.OUT2, M1.pin_1
  N3: Mod1.12V, Mod1.5V-ENA-JMP-I, Mod1.5V-ENA-JMP-O, VCC2.+
  GND: Mod1.GND, VCC2.-, Componente2.GND, HC-SR04_Sensor_1.GND, J1.gnd, R1.Pin_0, R2.Pin_0
  5V: Mod1.5V, Componente2.VIN
  N4: Mod1.OUT3, M2.pin_2
  N5: Mod1.OUT4, M2.pin_1
  N6: Mod1.ENA, Componente2.D6_PWM
  N7: Mod1.IN1, Componente2.D4
  N8: Mod1.IN2, Componente2.D5_PWM
  N9: Mod1.IN3, Componente2.D7
  N10: Mod1.IN4, Componente2.D8
  N11: Mod1.ENB, Componente2.D11_PWM/MOSI
  N12: Componente2.A0, LED2.anode
  N13: Componente2.A1, LED1.anode
  N14: Componente2.D9_PWM, J1.pulse
  N15: Componente2.D2, HC-SR04_Sensor_1.TRIG
  N16: Componente2.D3_PWM, HC-SR04_Sensor_1.ECHO
  VCC: Componente2.5V, HC-SR04_Sensor_1.VCC, J1.vcc
  N17: LED1.cathode, R2.Pin_1
  N18: LED2.cathode, R1.Pin_1

notes:
  Motor con Arduino, controlar dos
  motores a través de un L298N y Arduino, con dos salidas piloto para notificar el
  funcionamiento de cada motor activo

custom parts:
  L298N DC motor driver: 2x DC motor driver with 78M05 positive voltage regulator (7..35 V) L298N: max 46 V, 2 A Set 5 V Enable jumper to enable 5 V regultor (needed for the L298N) and +5 V output at screw terminal or supply external +5 V at screw terminal Set ENA and/or ENB to +5 V to enable motor permanently or supply ENA and/or ENB with PWM signal IN1 and IN2 set rotation directory for motor A (OUT1/OUT2) IN2 and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

// code stored in the sketch: esp-Motor.ino
// Motor 1
int motor1Pin1 = 13; 
int motor1Pin2 = 12; 
int enable1Pin = 15; 
int led1 = 22;
// Motor 2
int motor2Pin1 = 14; 
int motor2Pin2 = 27; 
int enable2Pin = 26; 
int led2 = 33;
int ciclo = 255;


void setup() {
  // put your setup code here, to run once:
  pinMode(motor1Pin1, OUTPUT);
  pinMode(motor1Pin2, OUTPUT);
  pinMode(enable1Pin, OUTPUT);
  pinMode(led1, OUTPUT);
  pinMode(motor2Pin1, OUTPUT);
  pinMode(motor2Pin2, OUTPUT);
  pinMode(enable2Pin, OUTPUT);
  pinMode(led2, OUTPUT);
  digitalWrite(led1, LOW);
  digitalWrite(led2, LOW);
  digitalWrite(motor1Pin1, LOW);
  digitalWrite(motor1Pin2, LOW);
  digitalWrite(motor2Pin1, LOW);
  digitalWrite(motor2Pin2, LOW);
  Serial.begin(9600);
  // testing
  Serial.print("Prueba Motor DC...");
}


void loop() {
  // put your main code here, to run repeatedly:
  // Motor Adelante
  Serial.println("Mover Adelante");
  digitalWrite(motor1Pin1, LOW);
  digitalWrite(motor1Pin2, HIGH);
  digitalWrite(motor2Pin1, LOW);
  digitalWrite(motor2Pin2, HIGH);  
  digitalWrite(led1, HIGH);
  digitalWrite(led2, LOW);
  delay(2000);
  // Motor Detenido
  Serial.println("Motor detenido");
  digitalWrite(motor1Pin1, LOW);
  digitalWrite(motor1Pin2, LOW);
  digitalWrite(motor2Pin1, LOW);
  digitalWrite(motor2Pin2, LOW); 
  digitalWrite(led1, LOW);
  digitalWrite(led2, LOW);
  delay(1000);
  // Motor Atras
  Serial.println("Mover Atras");
  digitalWrite(motor1Pin1, HIGH);
  digitalWrite(motor1Pin2, LOW);
  digitalWrite(motor2Pin1, HIGH);
  digitalWrite(motor2Pin2, LOW); 
  digitalWrite(led1, LOW);
  digitalWrite(led2, HIGH);
  delay(2000);
  // Motor Detenido
  Serial.println("Motor detenido");
  digitalWrite(motor1Pin1, LOW);
  digitalWrite(motor1Pin2, LOW);
  digitalWrite(motor2Pin1, LOW);
  digitalWrite(motor2Pin2, LOW); 
  digitalWrite(led1, LOW);
  digitalWrite(led2, LOW);
  delay(1000);
  // Motor incremental adelante
  Serial.println("Motor Incremental");
  digitalWrite(motor1Pin1, HIGH);
  digitalWrite(motor1Pin2, LOW);
  digitalWrite(motor2Pin1, HIGH);
  digitalWrite(motor2Pin2, LOW); 
  digitalWrite(led1, HIGH);
  digitalWrite(led2, LOW);
  for (int i=1;i<=ciclo;i++){
    analogWrite(enable1Pin, i);
    analogWrite(enable2Pin, i); 
    Serial.print("Adelante con velocidad: ");
    Serial.println(i);
  }
  delay(1000);
  // Motor Detenido
  Serial.println("Motor detenido");
  digitalWrite(motor1Pin1, LOW);
  digitalWrite(motor1Pin2, LOW);
  digitalWrite(motor2Pin1, LOW);
  digitalWrite(motor2Pin2, LOW); 
  digitalWrite(led1, LOW);
  digitalWrite(led2, LOW);
  delay(1000);
}
